# Fritzing sketch ROV Sensors (saved by Fritzing 0.9.3b)
circuit board: 8.46667cm x 5.64444cm
breadboards: 1

parts:
  Part1 = Arduino Mega 2560 (Rev3)
  U1 = Hirose DF13 Series Header [part_number=DF13#-4P-1.25V package=DF13C-4P-1.25V]
  Part3 = Bluetooth HC-05 Macho
  DHT1 = DHT11 Humitidy and Temperature Sensor
  R1 = Resistor [tolerance=±5% resistance=10k package=THT]
  Part4 = 9-DOF IMU L3GD20H + LSM303 [part_number=1714]

nets (from the schematic view):
  N1: Part1.D21/SCL, Part1.SCL
  N2: Part1.D20/SDA, Part1.SDA, U1.2, Part4.SDA
  N3: Part1.D10_PWM, Part3.RXD
  N4: Part1.D8_PWM, Part3.TXD
  GND: Part1.GND, U1.4, Part3.GND, DHT1.GND, Part4.GND
  N5: Part1.D2_PWM, DHT1.DATA, R1.Pin_0
  5V: Part1.5V, U1.1, Part3.VCC, DHT1.VDD, R1.Pin_1, Part4.VIN
  N6: U1.3, Part4.SCL

notes:
  5v side
  Sea Sweepers ROV

custom parts:
  DHT11 Humitidy and Temperature Sensor: DHT11 Humidity and Temperature Sensor
  9-DOF IMU L3GD20H + LSM303: This inertial-measurement-unit combines 2 of the best quality sensors available on the market to give you 9 axes of data: 3 axes of accelerometer data, 3 axes gyroscopic, and 3 axes magnetic (compass). We tested many different 'combination' sensors and found these were the best value, with stable and reliable readings.
